# Fritzing sketch circuit (saved by Fritzing 0.9.3b)
breadboards: 1

parts:
  Part1 = Arduino Mega 2560 (Rev3)
  DS1 = DS18B20 1-Wire Temperature Sensor [part_number=DS18B20]
  R1 = Resistor [tolerance=±5% resistance=4.7k package="0603 [SMD]"]
  U7 = Battery Holders [package=battery-aa-kit]
  U8 = Battery Holders [package=battery-aa-kit]
  U9 = Battery Holders [package=battery-aa-kit]
  U10 = Battery Holders [package=battery-aa-kit]
  U11 = Battery Holders [package=battery-aa-kit]
  U12 = Battery Holders [package=battery-aa-kit]
  U13 = Battery Holders [package=battery-aa-kit]
  U14 = Battery Holders [package=battery-aa-kit]
  U15 = Battery Holders [package=battery-aa-kit]
  U16 = Battery Holders [package=battery-aa-kit]
  U17 = Battery Holders [package=battery-aa-kit]
  U18 = Battery Holders [package=battery-aa-kit]
  U19 = Battery Holders [package=battery-aa-kit]
  U20 = Battery Holders [package=battery-aa-kit]
  U21 = Battery Holders [package=battery-aa-kit]
  U22 = Battery Holders [package=battery-aa-kit]
  U23 = Battery Holders [package=battery-aa-kit]
  U24 = Battery Holders [package=battery-aa-kit]
  U25 = Battery Holders [package=battery-aa-kit]
  U26 = Battery Holders [package=battery-aa-kit]
  U27 = Battery Holders [package=battery-aa-kit]
  U28 = Battery Holders [package=battery-aa-kit]
  U29 = Battery Holders [package=battery-aa-kit]
  U30 = Battery Holders [package=battery-aa-kit]
  Part3 = Analog Digital MUX Breakout
  Part2 = Analog Digital MUX Breakout
  R4 = Resistor [tolerance=±5% resistance=1k package="0603 [SMD]"]
  R5 = Resistor [tolerance=±5% resistance=22k package="0603 [SMD]"]
  R6 = Resistor [tolerance=±5% resistance=1k package="0603 [SMD]"]
  R7 = Resistor [tolerance=±5% resistance=47k package="0603 [SMD]"]
  R8 = Resistor [tolerance=±5% resistance=10k package="0603 [SMD]"]
  R9 = Resistor [tolerance=±5% resistance=100k package="0603 [SMD]"]
  R10 = Resistor [tolerance=±5% resistance=10k package="0603 [SMD]"]  # not connected
  F1 = FUSE [package=fuse_5mm]
  F2 = FUSE [package=fuse_5mm]
  F3 = FUSE [package=fuse_5mm]
  F4 = FUSE [package=fuse_5mm]
  F5 = FUSE [package=fuse_5mm]
  F6 = FUSE [package=fuse_5mm]
  F7 = FUSE [package=fuse_5mm]
  F8 = FUSE [package=fuse_5mm]
  F9 = FUSE [package=fuse_5mm]
  F10 = FUSE [package=fuse_5mm]
  F11 = FUSE [package=fuse_5mm]
  F12 = FUSE [package=fuse_5mm]
  F13 = FUSE [package=fuse_5mm]
  F14 = FUSE [package=fuse_5mm]
  F15 = FUSE [package=fuse_5mm]
  F16 = FUSE [package=fuse_5mm]
  F17 = FUSE [package=fuse_5mm]
  F18 = FUSE [package=fuse_5mm]
  F19 = FUSE [package=fuse_5mm]
  F20 = FUSE [package=fuse_5mm]
  F21 = FUSE [package=fuse_5mm]
  F22 = FUSE [package=fuse_5mm]
  F23 = FUSE [package=fuse_5mm]
  F24 = FUSE [package=fuse_5mm]

nets:
  N1: Part1.A1, R4.Pin_1, R5.Pin_0
  N2: Part1.A2, R6.Pin_1, R7.Pin_0
  N3: Part1.A3, R8.Pin_1, R9.Pin_0
  N4: Part1.D13_PWM, Part3.S0
  N5: Part1.D12_PWM, Part3.S1
  N6: Part1.D11_PWM, Part3.S2
  N7: Part1.D10_PWM, Part3.S3
  N8: Part1.D9_PWM, Part2.S0
  N9: Part1.D8_PWM, Part2.S1
  VCC: Part1.5V, DS1.DQ, DS1.VDD, R1.Pin_0, R1.Pin_1, Part3.VCC, Part2.VCC
  N10: Part1.D6_PWM, Part2.S3
  N11: Part1.D7_PWM, Part2.S2
  GND: Part1.GND, DS1.GND, Part3.GND, Part3.EN, Part2.GND, Part2.EN, R4.Pin_0, R6.Pin_0, R8.Pin_0
  N12: U7.+, F1.1
  N13: U7.-, U9.+, F2.1
  N14: U8.+, U9.-, F3.1
  N15: U8.-, U13.+, F4.1
  N16: U10.+, U13.-, F5.1
  N17: U10.-, U12.+, F6.1
  N18: U11.+, U12.-, F7.1
  N19: U11.-, U14.+, F8.1
  N20: U14.-, U16.+, F9.1
  N21: U15.+, U20.-, F13.1
  N22: U15.-, U22.+, F14.1
  N23: U16.-, U21.+, F10.1
  N24: U17.+, U18.-, F16.1
  N25: U17.-, U23.+, F24.1
  N26: U18.+, U22.-, F15.1
  N27: U19.+, U21.-, F11.1
  N28: U19.-, U20.+, F12.1
  N29: U23.-, U29.+, F23.1
  N30: U24.+, U27.-, F20.1
  N31: U24.-, U30.+, F19.1
  N32: U25.+, U30.-, F18.1
  N33: U25.-, U26.+, F17.1
  N34: U27.+, U28.-, F21.1
  N35: U28.+, U29.-, F22.1
  N36: Part3.C8, F17.2
  N37: Part3.C9, F18.2
  N38: Part3.C10, F19.2
  N39: Part3.C11, F20.2
  N40: Part3.C12, F21.2
  N41: Part3.C13, F22.2
  N42: Part3.C14, F23.2
  N43: Part3.C15, F24.2
  N44: Part2.C0, F16.2
  N45: Part2.C1, F15.2
  N46: Part2.C2, F14.2
  N47: Part2.C3, F13.2
  N48: Part2.C4, F12.2
  N49: Part2.C5, F11.2
  N50: Part2.C6, F10.2
  N51: Part2.C7, F9.2
  N52: Part2.C8, F8.2
  N53: Part2.C9, F7.2
  N54: Part2.C10, F6.2
  N55: Part2.C11, F5.2
  N56: Part2.C12, F4.2
  N57: Part2.C13, F3.2
  N58: Part2.C14, F2.2
  N59: Part2.C15, F1.2
